# Fritzing sketch smart-o-harp (saved by Fritzing 0.9.3b)
breadboards: 2

parts:
  IC1 = IC, SIP package, 8 pins [chip_label="12 buttons"]
  Power_plug1 = Power plug
  IC2 = SHIFT REGISTER [package=dil16]
  R2 = Resistor [tolerance=±5% resistance=1k package="2010 [SMD]"]
  R3 = Resistor [tolerance=±5% resistance=1k package="2010 [SMD]"]
  R4 = Resistor [tolerance=±5% resistance=1k package="2010 [SMD]"]
  R5 = Resistor [tolerance=±5% resistance=1k package="2010 [SMD]"]
  R6 = Resistor [tolerance=±5% resistance=1k package="2010 [SMD]"]
  R7 = Resistor [tolerance=±5% resistance=1k package="2010 [SMD]"]
  Q12 = NPN-Transistor [package="TO92 [THT]"]
  Q13 = NPN-Transistor [package="TO92 [THT]"]
  Q14 = NPN-Transistor [package="TO92 [THT]"]
  Q15 = NPN-Transistor [package="TO92 [THT]"]
  Q16 = NPN-Transistor [package="TO92 [THT]"]
  Q17 = NPN-Transistor [package="TO92 [THT]"]
  Q18 = NPN-Transistor [package="TO92 [THT]"]
  Q19 = NPN-Transistor [package="TO92 [THT]"]
  Q20 = NPN-Transistor [package="TO92 [THT]"]
  Q21 = NPN-Transistor [package="TO92 [THT]"]
  R9 = Resistor [tolerance=±5% resistance=1k package="2010 [SMD]"]
  R10 = Resistor [tolerance=±5% resistance=1k package="2010 [SMD]"]
  R11 = Resistor [tolerance=±5% resistance=1k package="2010 [SMD]"]
  R12 = Resistor [tolerance=±5% resistance=1k package="2010 [SMD]"]
  L1 = Solenoid
  L2 = Solenoid
  L3 = Solenoid
  IC3 = SHIFT REGISTER [package=dil16]
  Q22 = NPN-Transistor [package="TO92 [THT]"]
  Q23 = NPN-Transistor [package="TO92 [THT]"]
  R13 = Resistor [tolerance=±5% resistance=1k package="2010 [SMD]"]
  R14 = Resistor [tolerance=±5% resistance=1k package="2010 [SMD]"]
  L4 = Solenoid
  L5 = Solenoid
  L6 = Solenoid
  L7 = Solenoid
  L8 = Solenoid
  L9 = Solenoid
  L10 = Solenoid
  L11 = Solenoid
  L12 = Solenoid
  D1 = Rectifier Diode [part_number=1N4001 package="300 mil [THT]"]
  D2 = Rectifier Diode [part_number=1N4001 package="300 mil [THT]"]
  D3 = Rectifier Diode [part_number=1N4001 package="300 mil [THT]"]
  D4 = Rectifier Diode [part_number=1N4001 package="300 mil [THT]"]
  D5 = Rectifier Diode [part_number=1N4001 package="300 mil [THT]"]
  D6 = Rectifier Diode [part_number=1N4001 package="300 mil [THT]"]
  D7 = Rectifier Diode [part_number=1N4001 package="300 mil [THT]"]
  D8 = Rectifier Diode [part_number=1N4001 package="300 mil [THT]"]
  D9 = Rectifier Diode [part_number=1N4001 package="300 mil [THT]"]
  D10 = Rectifier Diode [part_number=1N4001 package="300 mil [THT]"]
  D11 = Rectifier Diode [part_number=1N4001 package="300 mil [THT]"]
  D12 = Rectifier Diode [part_number=1N4001 package="300 mil [THT]"]
  Part2 = Arduino Nano (Rev3.0)

nets:
  N1: IC1.pin1, Part2.D8
  N2: IC1.pin2, Part2.D7
  N3: IC1.pin3, Part2.D6
  N4: IC1.pin4, Part2.D5
  N5: IC1.pin5, Part2.D4
  N6: IC1.pin6, Part2.D3
  N7: IC1.pin7, Part2.D2
  GND: IC1.pin8, Power_plug1.GND, IC2.GND, IC2.G, Q12.E, Q13.E, Q13.C, Q14.E, Q15.E, Q16.E, Q17.E, Q18.E, Q19.E, Q20.E, Q21.E, L2.pin1, IC3.GND, IC3.G, Q22.E, Q23.E, D11.anode, Part2.GND
  VCC: Power_plug1.VCC, L1.pin2, L2.pin2, L3.pin2, L4.pin2, L5.pin2, L6.pin2, L7.pin2, L8.pin2, L9.pin2, L10.pin2, L11.pin2, L12.pin2, D1.cathode, D2.cathode, D3.cathode, D4.cathode, D5.cathode, D6.cathode, D7.cathode, D8.cathode, D9.cathode, D10.cathode, D11.cathode, D12.cathode, Part2.VIN
  N8: IC2.QB, R12.Pin_0
  N9: IC2.QC, R6.Pin_0
  N10: IC2.QD, R7.Pin_0
  N11: IC2.QE, R4.Pin_0
  N12: IC2.QF, R5.Pin_0
  N13: IC2.QG, R3.Pin_0
  N14: IC2.QH, R2.Pin_0
  VCC_2: IC2.SCL, IC2.VCC, IC3.SCL, IC3.VCC, Part2.5V
  N15: IC2.SCK, IC3.SCK, Part2.D12/MISO
  N16: IC2.RCK, IC3.RCK, Part2.D10
  N17: IC2.SER, IC3.QH*
  N18: IC2.QA, R10.Pin_0
  N19: R2.Pin_1, Q12.B
  N20: R3.Pin_1, Q13.B
  N21: R4.Pin_1, Q17.B
  N22: R5.Pin_1, Q14.B
  N23: R6.Pin_1, Q16.B
  N24: R7.Pin_1, Q15.B
  N25: Q12.C, L1.pin1, D12.anode
  N26: Q14.C, L3.pin1, D10.anode
  N27: Q15.C, L4.pin1, D8.anode
  N28: Q16.C, L6.pin1, D7.anode
  N29: Q17.C, L5.pin1, D9.anode
  N30: Q18.B, R12.Pin_1
  N31: Q18.C, L7.pin1, D6.anode
  N32: Q19.B, R9.Pin_1
  N33: Q19.C, L9.pin1, D4.anode
  N34: Q20.B, R11.Pin_1
  N35: Q20.C, L10.pin1, D3.anode
  N36: Q21.B, R10.Pin_1
  N37: Q21.C, L8.pin1, D5.anode
  N38: R9.Pin_0, IC3.QH
  N39: R11.Pin_0, IC3.QG
  N40: IC3.QE, R13.Pin_0
  N41: IC3.QF, R14.Pin_0
  N42: IC3.SER, Part2.D11/MOSI
  N43: Q22.B, R14.Pin_1
  N44: Q22.C, L11.pin1, D2.anode
  N45: Q23.B, R13.Pin_1
  N46: Q23.C, L12.pin1, D1.anode

notes:
  Solenoids: 12V DC spring push/pull 4mm.
  From experimentation, requires at least 70 mA to budge, draws about 120 mA if it can.
  12V 5A power supply
  Red wires are 12V
  Orange wires are 5V from arduino.
  Black wires are shared ground.
  The diodes prevent backwards current dischange when the solenoids turn off.
  12 outpus used.
  4 outputs extra*
  Power rail on this board: 5V
  12 Button keypad (with weird ground pin) right here
  Arduino Nano's pins, specs, and small size work very well
  2 8-bit shift registers in series
